// Logisim project branch_comp.circ as structural Verilog: 1 circuit, main circuit branch_comp
module branch_comp (
  input  [31:0] rs1,
  input  [31:0] rs2,
  input  BrUn,
  output BrEq,
  output BrLt
);

  wire not_1_out, SignedLt, UnsignedLt;

  Comparator #(.width(32)) comparator_1 (.a(rs1), .b(rs2), .lt(SignedLt));  // open: gt, eq
  Comparator #(.mode("unsigned"), .width(32)) comparator_2 (.a(rs1), .b(rs2), .eq(BrEq), .lt(UnsignedLt));  // open: gt
  assign BrLt = BrUn ? UnsignedLt : 1'bz;  // Controlled_Buffer controlled_buffer_1
  not not_1 (not_1_out, BrUn);
  assign BrLt = not_1_out ? SignedLt : 1'bz;  // Controlled_Buffer controlled_buffer_2

  // Notes on the sheet:
  //   INPUTS to your circuit
  //   unsigned comparison performed when BrUn == 1
  //   DON'T CHANGE THE LOCATIONS OF THE INPUTS AND OUTPUTS!
  //   OUTPUT from your circuit
endmodule
