// Logisim project control_logic.circ as structural Verilog: 1 circuit, main circuit control_logic
module control_logic (
  input  [31:0] inst,
  input  BrEq,
  input  BrLt,
  output PCSel,
  output RegWEn,
  output [2:0] ImmSel,
  output BrUn,
  output ASel,
  output BSel,
  output [3:0] ALUSel,
  output MemRW,
  output [1:0] WBSel,
  output CSRSel,
  output CSRWen
);

  wire and_1_out, and_2_out, and_3_out, and_4_out, and_5_out, and_6_out, and_7_out, and_8_out, and_9_out,
       and_10_out, and_11_out, and_12_out, and_13_out, and_14_out, and_15_out, and_16_out, and_17_out,
       and_18_out, and_19_out, and_20_out, and_21_out, and_22_out, and_23_out, and_24_out, and_25_out,
       and_26_out, and_27_out, and_28_out, and_29_out, auipc, BranchGreaterorEqual, BranchNotEqual,
       comparator_11_eq, comparator_12_eq, comparator_13_eq, comparator_14_eq, comparator_15_eq,
       comparator_16_eq, comparator_17_eq, comparator_18_eq, comparator_19_eq, comparator_20_eq,
       comparator_21_eq, comparator_22_eq, comparator_23_eq, comparator_24_eq, comparator_25_eq,
       comparator_26_eq, comparator_27_eq, comparator_28_eq, comparator_29_eq, comparator_30_eq,
       comparator_31_eq, comparator_32_eq, comparator_33_eq, comparator_34_eq, comparator_35_eq,
       comparator_36_eq, comparator_37_eq, comparator_38_eq, comparator_39_eq, comparator_40_eq,
       comparator_41_eq, comparator_42_eq, comparator_43_eq, comparator_44_eq, CsrWrite, IArth, IType, jalr,
       LoadType, lui, not_2_out, not_3_out, not_4_out, not_5_out, not_6_out, not_7_out, not_8_out, not_9_out,
       not_10_out, or_3_out, or_5_out, or_6_out, or_7_out, or_8_out, or_9_out, or_10_out, or_11_out,
       or_12_out, or_13_out, or_14_out, or_15_out, or_16_out, or_17_out, or_18_out, or_19_out, or_20_out,
       or_21_out, RType, SBType, SType, UJType, UType;

  not not_1 (BranchNotEqual, BrEq);
  not not_2 (not_2_out, BrEq);
  not not_3 (not_3_out, BrLt);
  Comparator #(.width(7)) comparator_1 (.a(inst[6:0]), .b(7'b0000011), .eq(LoadType));  // open: gt, lt
  Comparator #(.width(7)) comparator_2 (.a(inst[6:0]), .b(7'b0010011), .eq(IArth));  // open: gt, lt
  Comparator #(.width(7)) comparator_3 (.a(inst[6:0]), .b(7'b1100111), .eq(jalr));  // open: gt, lt
  Comparator #(.width(7)) comparator_4 (.a(inst[6:0]), .b(7'b1110011), .eq(CsrWrite));  // open: gt, lt
  Comparator #(.width(7)) comparator_5 (.a(inst[6:0]), .b(7'b0100011), .eq(SType));  // open: gt, lt
  Comparator #(.width(7)) comparator_6 (.a(inst[6:0]), .b(7'b1100011), .eq(SBType));  // open: gt, lt
  Comparator #(.width(7)) comparator_7 (.a(inst[6:0]), .b(7'b0010111), .eq(auipc));  // open: gt, lt
  Comparator #(.width(7)) comparator_8 (.a(inst[6:0]), .b(7'b0110111), .eq(lui));  // open: gt, lt
  Comparator #(.width(7)) comparator_9 (.a(inst[6:0]), .b(7'b1101111), .eq(UJType));  // open: gt, lt
  Comparator #(.width(7)) comparator_10 (.a(inst[6:0]), .b(7'b0110011), .eq(RType));  // open: gt, lt
  Comparator #(.width(3)) comparator_11 (.a(inst[14:12]), .b(3'b110), .eq(comparator_11_eq));  // open: gt, lt
  Comparator #(.width(3)) comparator_12 (.a(inst[14:12]), .b(3'b111), .eq(comparator_12_eq));  // open: gt, lt
  or or_1 (BranchGreaterorEqual, BrEq, and_1_out);
  and and_1 (and_1_out, not_2_out, not_3_out);
  or or_2 (UType, auipc, lui);
  assign BrUn = or_3_out ? 1'b1 : 1'bz;  // Controlled_Buffer controlled_buffer_1
  or or_3 (or_3_out, comparator_11_eq, comparator_12_eq);
  not not_4 (not_4_out, or_3_out);
  assign BrUn = not_4_out ? 1'b0 : 1'bz;  // Controlled_Buffer controlled_buffer_2
  or or_4 (IType, LoadType, IArth, jalr, CsrWrite);
  assign ImmSel = IType ? 3'b000 : 3'bz;  // Controlled_Buffer controlled_buffer_3
  assign ImmSel = SType ? 3'b001 : 3'bz;  // Controlled_Buffer controlled_buffer_4
  assign ImmSel = SBType ? 3'b010 : 3'bz;  // Controlled_Buffer controlled_buffer_5
  assign ImmSel = UType ? 3'b011 : 3'bz;  // Controlled_Buffer controlled_buffer_6
  assign ImmSel = UJType ? 3'b100 : 3'bz;  // Controlled_Buffer controlled_buffer_7
  or or_5 (or_5_out, IType, SType, RType);
  assign ASel = or_5_out ? 1'b0 : 1'bz;  // Controlled_Buffer controlled_buffer_8
  assign ASel = or_6_out ? 1'b1 : 1'bz;  // Controlled_Buffer controlled_buffer_9
  or or_6 (or_6_out, UType, SBType, UJType);
  assign BSel = RType ? 1'b0 : 1'bz;  // Controlled_Buffer controlled_buffer_10
  assign BSel = or_7_out ? 1'b1 : 1'bz;  // Controlled_Buffer controlled_buffer_11
  or or_7 (or_7_out, UJType, UType, IType, SType, SBType);
  Comparator #(.width(3)) comparator_13 (.a(inst[14:12]), .b(3'b101), .eq(comparator_13_eq));  // open: gt, lt
  not not_5 (not_5_out, BrUn);
  Comparator #(.width(3)) comparator_14 (.a(inst[14:12]), .b(3'b100), .eq(comparator_14_eq));  // open: gt, lt
  not not_6 (not_6_out, BrUn);
  Comparator #(.width(3)) comparator_15 (.a(inst[14:12]), .b(3'b000), .eq(comparator_15_eq));  // open: gt, lt
  Comparator #(.width(3)) comparator_16 (.a(inst[14:12]), .b(3'b001), .eq(comparator_16_eq));  // open: gt, lt
  Comparator #(.width(3)) comparator_17 (.a(inst[14:12]), .b(3'b110), .eq(comparator_17_eq));  // open: gt, lt
  Comparator #(.width(3)) comparator_18 (.a(inst[14:12]), .b(3'b111), .eq(comparator_18_eq));  // open: gt, lt
  and and_2 (and_2_out, comparator_13_eq, not_5_out, BranchGreaterorEqual);
  and and_3 (and_3_out, comparator_14_eq, not_6_out, BrLt);
  and and_4 (and_4_out, comparator_15_eq, BrEq);
  and and_5 (and_5_out, comparator_16_eq, BranchNotEqual);
  and and_6 (and_6_out, comparator_17_eq, BrUn, BrLt);
  and and_7 (and_7_out, comparator_18_eq, BrUn, BranchGreaterorEqual);
  not not_7 (not_7_out, CsrWrite);
  assign CSRWen = 1'b1 ? CsrWrite : 1'bz;  // Controlled_Buffer controlled_buffer_12
  assign CSRWen = 1'b0 ? not_7_out : 1'bz;  // Controlled_Buffer controlled_buffer_13
  assign RegWEn = not_8_out ? 1'b0 : 1'bz;  // Controlled_Buffer controlled_buffer_14
  not not_8 (not_8_out, or_8_out);
  or or_8 (or_8_out, IType, UType, UJType, RType);
  or or_9 (or_9_out, IArth, UType, CsrWrite, RType);
  assign WBSel = or_9_out ? 2'b01 : 2'bz;  // Controlled_Buffer controlled_buffer_15
  assign WBSel = LoadType ? 2'b00 : 2'bz;  // Controlled_Buffer controlled_buffer_16
  assign WBSel = or_10_out ? 2'b10 : 2'bz;  // Controlled_Buffer controlled_buffer_17
  or or_10 (or_10_out, jalr, UJType);
  or or_11 (or_11_out, and_2_out, and_3_out, and_4_out, and_5_out, and_6_out, and_7_out);
  not not_9 (not_9_out, SType);
  assign RegWEn = or_8_out ? 1'b1 : 1'bz;  // Controlled_Buffer controlled_buffer_18
  Comparator #(.width(3)) comparator_19 (.a(inst[14:12]), .b(3'b001), .eq(comparator_19_eq));  // open: gt, lt
  assign CSRSel = comparator_19_eq ? 1'b1 : 1'bz;  // Controlled_Buffer controlled_buffer_19
  assign CSRSel = comparator_20_eq ? 1'b0 : 1'bz;  // Controlled_Buffer controlled_buffer_20
  Comparator #(.width(3)) comparator_20 (.a(inst[14:12]), .b(3'b101), .eq(comparator_20_eq));  // open: gt, lt
  and and_8 (and_8_out, or_11_out, SBType);
  assign MemRW = 1'b1 ? SType : 1'bz;  // Controlled_Buffer controlled_buffer_21
  assign MemRW = 1'b0 ? not_9_out : 1'bz;  // Controlled_Buffer controlled_buffer_22
  assign PCSel = or_12_out ? 1'b1 : 1'bz;  // Controlled_Buffer controlled_buffer_23
  or or_12 (or_12_out, jalr, and_8_out, UJType);
  not not_10 (not_10_out, or_12_out);
  assign PCSel = not_10_out ? 1'b0 : 1'bz;  // Controlled_Buffer controlled_buffer_24
  and and_9 (and_9_out, RType, comparator_21_eq);
  Comparator #(.width(7)) comparator_21 (.a(inst[31:25]), .b({7{1'b0}}), .eq(comparator_21_eq));  // open: gt, lt
  and and_10 (and_10_out, RType, comparator_22_eq);
  Comparator #(.width(7)) comparator_22 (.a(inst[31:25]), .b({7{1'b0}}), .eq(comparator_22_eq));  // open: gt, lt
  and and_11 (and_11_out, RType, comparator_23_eq);
  Comparator #(.width(7)) comparator_23 (.a(inst[31:25]), .b({7{1'b0}}), .eq(comparator_23_eq));  // open: gt, lt
  and and_12 (and_12_out, RType, comparator_24_eq);
  Comparator #(.width(7)) comparator_24 (.a(inst[31:25]), .b({7{1'b0}}), .eq(comparator_24_eq));  // open: gt, lt
  or or_13 (or_13_out, IArth, and_9_out);
  Comparator #(.width(3)) comparator_25 (.a(inst[14:12]), .b(3'b100), .eq(comparator_25_eq));  // open: gt, lt
  or or_14 (or_14_out, IArth, and_10_out);
  Comparator #(.width(3)) comparator_26 (.a(inst[14:12]), .b(3'b110), .eq(comparator_26_eq));  // open: gt, lt
  or or_15 (or_15_out, IArth, and_11_out);
  Comparator #(.width(3)) comparator_27 (.a(inst[14:12]), .b(3'b111), .eq(comparator_27_eq));  // open: gt, lt
  or or_16 (or_16_out, IArth, and_12_out);
  Comparator #(.width(3)) comparator_28 (.a(inst[14:12]), .b(3'b010), .eq(comparator_28_eq));  // open: gt, lt
  and and_13 (and_13_out, or_13_out, comparator_25_eq);
  assign ALUSel = and_13_out ? 4'b0011 : 4'bz;  // Controlled_Buffer controlled_buffer_25
  and and_14 (and_14_out, or_14_out, comparator_26_eq);
  assign ALUSel = and_14_out ? 4'b0010 : 4'bz;  // Controlled_Buffer controlled_buffer_26
  and and_15 (and_15_out, or_15_out, comparator_27_eq);
  assign ALUSel = and_15_out ? 4'b0001 : 4'bz;  // Controlled_Buffer controlled_buffer_27
  and and_16 (and_16_out, or_16_out, comparator_28_eq);
  assign ALUSel = and_16_out ? 4'b0111 : 4'bz;  // Controlled_Buffer controlled_buffer_28
  and and_17 (and_17_out, RType, comparator_29_eq);
  Comparator #(.width(7)) comparator_29 (.a(inst[31:25]), .b({7{1'b0}}), .eq(comparator_29_eq));  // open: gt, lt
  or or_17 (or_17_out, IArth, and_17_out);
  Comparator #(.width(3)) comparator_30 (.a(inst[14:12]), .b(3'b000), .eq(comparator_30_eq));  // open: gt, lt
  or or_18 (or_18_out, IArth, RType);
  and and_18 (and_18_out, or_18_out, comparator_31_eq, comparator_32_eq);
  Comparator #(.width(7)) comparator_31 (.a(inst[31:25]), .b({7{1'b0}}), .eq(comparator_31_eq));  // open: gt, lt
  Comparator #(.width(3)) comparator_32 (.a(inst[14:12]), .b(3'b101), .eq(comparator_32_eq));  // open: gt, lt
  or or_19 (or_19_out, IArth, RType);
  and and_19 (and_19_out, or_19_out, comparator_33_eq, comparator_34_eq);
  Comparator #(.width(7)) comparator_33 (.a(inst[31:25]), .b(7'b0100000), .eq(comparator_33_eq));  // open: gt, lt
  Comparator #(.width(3)) comparator_34 (.a(inst[14:12]), .b(3'b101), .eq(comparator_34_eq));  // open: gt, lt
  or or_20 (or_20_out, IArth, RType);
  and and_20 (and_20_out, or_20_out, comparator_35_eq, comparator_36_eq);
  Comparator #(.width(7)) comparator_35 (.a(inst[31:25]), .b({7{1'b0}}), .eq(comparator_35_eq));  // open: gt, lt
  Comparator #(.width(3)) comparator_36 (.a(inst[14:12]), .b(3'b001), .eq(comparator_36_eq));  // open: gt, lt
  and and_21 (and_21_out, or_17_out, comparator_30_eq);
  assign ALUSel = and_18_out ? 4'b0100 : 4'bz;  // Controlled_Buffer controlled_buffer_29
  assign ALUSel = and_19_out ? 4'b0101 : 4'bz;  // Controlled_Buffer controlled_buffer_30
  assign ALUSel = and_20_out ? 4'b0110 : 4'bz;  // Controlled_Buffer controlled_buffer_31
  or or_21 (or_21_out, auipc, SType, LoadType, and_21_out, SBType, UJType, jalr);
  assign ALUSel = or_21_out ? 4'b0000 : 4'bz;  // Controlled_Buffer controlled_buffer_32
  assign ALUSel = lui ? 4'b1101 : 4'bz;  // Controlled_Buffer controlled_buffer_33
  Comparator #(.width(7)) comparator_37 (.a(inst[31:25]), .b(7'b0000001), .eq(comparator_37_eq));  // open: gt, lt
  Comparator #(.width(7)) comparator_38 (.a(inst[31:25]), .b(7'b0100000), .eq(comparator_38_eq));  // open: gt, lt
  Comparator #(.width(7)) comparator_39 (.a(inst[31:25]), .b(7'b0000001), .eq(comparator_39_eq));  // open: gt, lt
  Comparator #(.width(7)) comparator_40 (.a(inst[31:25]), .b(7'b0000001), .eq(comparator_40_eq));  // open: gt, lt
  and and_22 (and_22_out, RType, comparator_37_eq);
  and and_23 (and_23_out, and_22_out, comparator_41_eq);
  Comparator #(.width(3)) comparator_41 (.a(inst[14:12]), .b(3'b000), .eq(comparator_41_eq));  // open: gt, lt
  and and_24 (and_24_out, RType, comparator_38_eq);
  and and_25 (and_25_out, and_24_out, comparator_42_eq);
  Comparator #(.width(3)) comparator_42 (.a(inst[14:12]), .b(3'b000), .eq(comparator_42_eq));  // open: gt, lt
  and and_26 (and_26_out, RType, comparator_39_eq);
  and and_27 (and_27_out, and_26_out, comparator_43_eq);
  Comparator #(.width(3)) comparator_43 (.a(inst[14:12]), .b(3'b001), .eq(comparator_43_eq));  // open: gt, lt
  and and_28 (and_28_out, RType, comparator_40_eq);
  and and_29 (and_29_out, and_28_out, comparator_44_eq);
  Comparator #(.width(3)) comparator_44 (.a(inst[14:12]), .b(3'b011), .eq(comparator_44_eq));  // open: gt, lt
  assign ALUSel = and_23_out ? 4'b1010 : 4'bz;  // Controlled_Buffer controlled_buffer_34
  assign ALUSel = and_25_out ? 4'b1100 : 4'bz;  // Controlled_Buffer controlled_buffer_35
  assign ALUSel = and_27_out ? 4'b1110 : 4'bz;  // Controlled_Buffer controlled_buffer_36
  assign ALUSel = and_29_out ? 4'b1011 : 4'bz;  // Controlled_Buffer controlled_buffer_37

  // Other names for the same wires on the sheet: BranchEQual = BrEq; BranchLessThan = BrLt; opcode[6:0] = inst[6:0];
  //   rd[4:0] = inst[11:7]; funct3[2:0] = inst[14:12]; rs1[4:0] = inst[19:15]; rs2[4:0] = inst[24:20];
  //   funct7[6:0] = inst[31:25]

  // Notes on the sheet:
  //   INPUTS to your circuit
  //   not implemented
  //   not implemented
  //   not implemented
  //   DON'T CHANGE THE LOCATIONS OF THE INPUTS AND OUTPUTS!
  //   OUTPUT from your circuit
  //   0 for rs1, 1 for PC
  //   0 for rs2, 1 for imm_gen
  //   xor
  //   or
  //   and
  //   slt
  //   add
  //   srl
  //   sra
  //   sll
  //   mul
  //   sub
  //   mulh
  //   mulhu
endmodule
