// Logisim project cpu.circ as structural Verilog: 1 circuit, main circuit cpu
module cpu (
  input  clk,
  input  [31:0] INSTRUCTION,
  input  [31:0] READ_DATA,
  output [31:0] WRITE_ADDRESS,
  output [31:0] PROGRAM_COUNTER,
  output [31:0] ra,
  output [31:0] sp,
  output [31:0] t0,
  output [31:0] t1,
  output [31:0] t2,
  output [31:0] s0,
  output [31:0] s1,
  output [31:0] a0,
  output [31:0] tohost,
  output [3:0] WRITE_ENABLE,
  output [31:0] WRITE_DATA
);

  wire ASel, BeEq, BrLt, BrUn, BSel, comparator_1_eq, comparator_2_eq, comparator_3_eq, CSRSel, CSRWen,
       MemRW, not_1_out, not_2_out, not_3_out, not_4_out, not_5_out, PCSel, RWE;
  wire [1:0] WBSel;
  wire [2:0] funct3, ImmSel;
  wire [3:0] ALUSel, MemMask;
  wire [6:0] funct7, opcode;
  wire [24:7] Phase2_Inst;
  wire [31:0] adder_1_out, adder_2_out, bit_extender_1_out, DMEM_Output, Generated_imm, multiplexer_1_out,
       multiplexer_2_out, multiplexer_3_out, multiplexer_4_out, multiplexer_5_out, Phase2_PC, rs_1,
       Writeback_Data;

  Adder #(.width(32)) adder_1 (.a(PROGRAM_COUNTER), .b(32'h4), .out(adder_1_out));  // open: cin, cout
  Multiplexer #(.enable("false"), .width(32)) multiplexer_1 (
    .in0(adder_1_out), .in1(WRITE_ADDRESS), .out(multiplexer_1_out), .sel(PCSel));
  Register #(.width(32)) PC (.D(multiplexer_1_out), .clk(clk), .Q(PROGRAM_COUNTER));  // open: en, clr
  Multiplexer #(.enable("false"), .width(32)) multiplexer_2 (
    .in0(INSTRUCTION), .in1(32'h13), .out(multiplexer_2_out), .sel(PCSel));
  Register #(.width(32)) Pipeline_PC_Reg (.D(PROGRAM_COUNTER), .en(1'b1), .clk(clk), .Q(Phase2_PC));  // open: clr
  Register #(.width(32)) Pipeline_Inst_Reg (
    .D(multiplexer_2_out), .en(1'b1), .clk(clk),
    .Q({funct7, Phase2_Inst[24:15], funct3, Phase2_Inst[11:7], opcode}));  // open: clr
  control_logic control_logic_1 (
    .CSRWen(CSRWen), .PCSel(PCSel), .RegWEn(RWE), .ImmSel(ImmSel), .BrUn(BrUn), .ASel(ASel), .BSel(BSel),
    .ALUSel(ALUSel), .MemRW(MemRW), .WBSel(WBSel), .CSRSel(CSRSel),
    .inst({funct7, Phase2_Inst[24:15], funct3, Phase2_Inst[11:7], opcode}), .BrEq(BeEq), .BrLt(BrLt));
  regfile regfile_1 (
    .rs1(Phase2_Inst[19:15]), .rs2(Phase2_Inst[24:20]), .rd(Phase2_Inst[11:7]), .Write_Data(Writeback_Data),
    .RegWEn(RWE), .clk(clk), .ra(ra), .sp(sp), .t0(t0), .t1(t1), .t2(t2), .s0(s0), .s1(s1), .a0(a0),
    .Read_Data_1(rs_1), .Read_Data_2(WRITE_DATA));
  imm_gen imm_gen_1 (
    .inst({funct7, Phase2_Inst[24:15], funct3, Phase2_Inst[11:7], opcode}), .ImmSel(ImmSel),
    .imm(Generated_imm));
  Multiplexer #(.enable("false"), .width(32)) multiplexer_3 (
    .in0(rs_1), .in1(Phase2_PC), .out(multiplexer_3_out), .sel(ASel));
  Multiplexer #(.enable("false"), .width(32)) multiplexer_4 (
    .in0(WRITE_DATA), .in1(Generated_imm), .out(multiplexer_4_out), .sel(BSel));
  alu alu_1 (.Result(WRITE_ADDRESS), .A(multiplexer_3_out), .B(multiplexer_4_out), .ALUSel(ALUSel));
  branch_comp branch_comp_1 (.rs1(rs_1), .rs2(WRITE_DATA), .BrUn(BrUn), .BrEq(BrLt), .BrLt(BeEq));
  assign bit_extender_1_out = {{27{1'b0}}, Phase2_Inst[19:15]};  // Bit_Extender bit_extender_1
  Comparator #(.mode("unsigned"), .width(3)) comparator_1 (
    .a(funct3), .b(3'b010), .eq(comparator_1_eq));  // open: gt, lt
  assign MemMask = comparator_1_eq ? 4'b1111 : 4'bz;  // Controlled_Buffer controlled_buffer_1
  assign WRITE_ENABLE = MemRW ? MemMask : 4'bz;  // Controlled_Buffer controlled_buffer_2
  not not_1 (not_1_out, MemRW);
  assign WRITE_ENABLE = not_1_out ? 4'b0000 : 4'bz;  // Controlled_Buffer controlled_buffer_3
  Multiplexer #(.enable("false"), .width(32)) multiplexer_5 (
    .in0(bit_extender_1_out), .in1(rs_1), .out(multiplexer_5_out), .sel(CSRSel));
  Comparator #(.mode("unsigned"), .width(3)) comparator_2 (
    .a(funct3), .b(3'b001), .eq(comparator_2_eq));  // open: gt, lt
  assign MemMask = comparator_2_eq ? 4'b0011 : 4'bz;  // Controlled_Buffer controlled_buffer_4
  csr csr_1 (
    .CSR_address(Generated_imm[11:0]), .CSR_din(multiplexer_5_out), .CSR_WE(CSRWen), .clk(clk),
    .tohost(tohost));
  Comparator #(.mode("unsigned"), .width(3)) comparator_3 (
    .a(funct3), .b(3'b000), .eq(comparator_3_eq));  // open: gt, lt
  not not_2 (not_2_out, MemMask[0]);
  not not_3 (not_3_out, MemMask[1]);
  assign DMEM_Output[7:0] = MemMask[0] ? READ_DATA[7:0] : 8'bz;  // Controlled_Buffer controlled_buffer_5
  assign DMEM_Output[7:0] = not_2_out ? {8{1'b0}} : 8'bz;  // Controlled_Buffer controlled_buffer_6
  assign DMEM_Output[15:8] = MemMask[1] ? READ_DATA[15:8] : 8'bz;  // Controlled_Buffer controlled_buffer_7
  assign DMEM_Output[15:8] = not_3_out ? {8{1'b0}} : 8'bz;  // Controlled_Buffer controlled_buffer_8
  assign MemMask = comparator_3_eq ? 4'b0001 : 4'bz;  // Controlled_Buffer controlled_buffer_9
  not not_4 (not_4_out, MemMask[2]);
  not not_5 (not_5_out, MemMask[3]);
  assign DMEM_Output[23:16] = MemMask[2] ? READ_DATA[23:16] : 8'bz;  // Controlled_Buffer controlled_buffer_10
  assign DMEM_Output[23:16] = not_4_out ? {8{1'b0}} : 8'bz;  // Controlled_Buffer controlled_buffer_11
  assign DMEM_Output[31:24] = MemMask[3] ? READ_DATA[31:24] : 8'bz;  // Controlled_Buffer controlled_buffer_12
  assign DMEM_Output[31:24] = not_5_out ? {8{1'b0}} : 8'bz;  // Controlled_Buffer controlled_buffer_13
  // Probe on DMEM_Output
  Adder #(.width(32)) adder_2 (.a(Phase2_PC), .b(32'h4), .out(adder_2_out));  // open: cin, cout
  Multiplexer #(.enable("false"), .select(2), .width(32)) multiplexer_6 (
    .in0(DMEM_Output), .in1(WRITE_ADDRESS), .in2(adder_2_out), .out(Writeback_Data), .sel(WBSel));  // open: in3

  // Other names for the same wires on the sheet: ALU_Output[31:0] = WRITE_ADDRESS;
  //   Phase2_Inst (some bits) = {funct7, funct3, opcode}; rd[4:0] = Phase2_Inst[11:7]; rs1[4:0] = Phase2_Inst[19:15];
  //   rs2[4:0] = Phase2_Inst[24:20]; rs_2[31:0] = WRITE_DATA

  // Notes on the sheet:
  //   Output to IMEM
  //   IMEM (do **NOT** move this)
  //   Inputs from IMEM
  //   It is OK to move the PC, RegFile, ALU, MEM, Branch Comp, Imm Gen, and Control Logic to wherever is most convenient for you when constructing your CPU, and to delete this text
  //   Inputs/Outputs for testing. Do **NOT** move these.
  //   Outputs To DMEM
  //   DMEM (do **NOT** move this)
  //   Inputs From DMEM
  //   pesudo DMEM
endmodule
