// Logisim project imm_gen.circ as structural Verilog: 1 circuit, main circuit imm_gen
module imm_gen (
  input  [31:0] inst,
  input  [2:0] ImmSel,
  output [31:0] imm
);

  wire [31:0] IType, SBType, SType, UJType;

  // Probe on inst[31:20]
  // Probe on {inst[31:25], inst[11:7]}
  // Probe on IType
  assign IType = {{20{inst[31]}}, inst[31:20]};  // Bit_Extender bit_extender_1
  // Probe on SType
  assign SType = {{20{inst[31]}}, {inst[31:25], inst[11:7]}};  // Bit_Extender bit_extender_2
  // Probe on {inst[31:12], {12{1'b0}}}
  Multiplexer #(.enable("false"), .select(3), .width(32)) multiplexer_1 (
    .in0(IType), .in1(SType), .in2(SBType), .in3({inst[31:12], {12{1'b0}}}), .in4(UJType), .out(imm),
    .sel(ImmSel));  // open: in5, in6, in7
  assign UJType = {{11{inst[31]}}, {inst[31], inst[19:12], inst[20], inst[30:21], 1'b0}};  // Bit_Extender bit_extender_3
  assign SBType = {{19{inst[31]}}, {inst[31], inst[7], inst[30:25], inst[11:8], 1'b0}};  // Bit_Extender bit_extender_4

  // Other names for the same wires on the sheet: rd[4:0] = inst[11:7]; SB_imm_4_1[3:0] = inst[11:8];
  //   funct7[6:0] = inst[31:25]; SB_imm_10_5[5:0] = inst[30:25]; UJ_imm_10_1[9:0] = inst[30:21];
  //   UType[31:12] = inst[31:12]; SB_imm_11 = inst[7]; SB_imm_12 = inst[31]; UJ_imm_20 = inst[31];
  //   rs2[4:0] = inst[24:20]; UJ_imm_11 = inst[20]; funct3[2:0] = inst[14:12]; UJ_imm_19_12[7:0] = inst[19:12];
  //   rs1[4:0] = inst[19:15]; opcode[6:0] = inst[6:0]

  // Notes on the sheet:
  //   INPUTS to your circuit
  //   DON'T CHANGE THE LOCATIONS OF THE INPUTS AND OUTPUTS!
  //   0:I, 1:S, 2:SB, 3:U, 4:UJ
  //   OUTPUT from your circuit
endmodule
