// Logisim project regfile.circ as structural Verilog: 1 circuit, main circuit regfile
module regfile (
  input  [4:0] rs1,
  input  [4:0] rs2,
  input  [4:0] rd,
  input  [31:0] Write_Data,
  input  RegWEn,
  input  clk,
  output [31:0] ra,
  output [31:0] sp,
  output [31:0] t0,
  output [31:0] t1,
  output [31:0] t2,
  output [31:0] s0,
  output [31:0] s1,
  output [31:0] a0,
  output [31:0] Read_Data_1,
  output [31:0] Read_Data_2
);

  wire wen_0, wen_1, wen_2, wen_3, wen_4, wen_5, wen_6, wen_7, wen_8, wen_9, wen_10, wen_11, wen_12, wen_13,
       wen_14, wen_15, wen_16, wen_17, wen_18, wen_19, wen_20, wen_21, wen_22, wen_23, wen_24, wen_25,
       wen_26, wen_27, wen_28, wen_29, wen_30, wen_31;
  wire [31:0] out0, out3, out4, out11, out12, out13, out14, out15, out16, out17, out18, out19, out20, out21,
       out22, out23, out24, out25, out26, out27, out28, out29, out30, out31;

  Register #(.width(32)) x0 (.D({32{1'b0}}), .en(wen_0), .clk(clk), .Q(out0));  // open: clr
  Register #(.width(32)) x4 (.D(Write_Data), .en(wen_4), .clk(clk), .Q(out4));  // open: clr
  Register #(.width(32)) x8 (.D(Write_Data), .en(wen_8), .clk(clk), .Q(s0));  // open: clr
  Register #(.width(32)) x12 (.D(Write_Data), .en(wen_12), .clk(clk), .Q(out12));  // open: clr
  Register #(.width(32)) x16 (.D(Write_Data), .en(wen_16), .clk(clk), .Q(out16));  // open: clr
  Register #(.width(32)) x20 (.D(Write_Data), .en(wen_20), .clk(clk), .Q(out20));  // open: clr
  Register #(.width(32)) x24 (.D(Write_Data), .en(wen_24), .clk(clk), .Q(out24));  // open: clr
  Register #(.width(32)) x28 (.D(Write_Data), .en(wen_28), .clk(clk), .Q(out28));  // open: clr
  Register #(.width(32)) x1 (.D(Write_Data), .en(wen_1), .clk(clk), .Q(ra));  // open: clr
  Register #(.width(32)) x5 (.D(Write_Data), .en(wen_5), .clk(clk), .Q(t0));  // open: clr
  Register #(.width(32)) x9 (.D(Write_Data), .en(wen_9), .clk(clk), .Q(s1));  // open: clr
  Register #(.width(32)) x13 (.D(Write_Data), .en(wen_13), .clk(clk), .Q(out13));  // open: clr
  Register #(.width(32)) x17 (.D(Write_Data), .en(wen_17), .clk(clk), .Q(out17));  // open: clr
  Register #(.width(32)) x21 (.D(Write_Data), .en(wen_21), .clk(clk), .Q(out21));  // open: clr
  Register #(.width(32)) x25 (.D(Write_Data), .en(wen_25), .clk(clk), .Q(out25));  // open: clr
  Register #(.width(32)) x29 (.D(Write_Data), .en(wen_29), .clk(clk), .Q(out29));  // open: clr
  Register #(.width(32)) x2 (.D(Write_Data), .en(wen_2), .clk(clk), .Q(sp));  // open: clr
  Register #(.width(32)) x6 (.D(Write_Data), .en(wen_6), .clk(clk), .Q(t1));  // open: clr
  Register #(.width(32)) x10 (.D(Write_Data), .en(wen_10), .clk(clk), .Q(a0));  // open: clr
  Register #(.width(32)) x14 (.D(Write_Data), .en(wen_14), .clk(clk), .Q(out14));  // open: clr
  Register #(.width(32)) x18 (.D(Write_Data), .en(wen_18), .clk(clk), .Q(out18));  // open: clr
  Register #(.width(32)) x22 (.D(Write_Data), .en(wen_22), .clk(clk), .Q(out22));  // open: clr
  Register #(.width(32)) x26 (.D(Write_Data), .en(wen_26), .clk(clk), .Q(out26));  // open: clr
  Register #(.width(32)) x30 (.D(Write_Data), .en(wen_30), .clk(clk), .Q(out30));  // open: clr
  Register #(.width(32)) x3 (.D(Write_Data), .en(wen_3), .clk(clk), .Q(out3));  // open: clr
  Register #(.width(32)) x7 (.D(Write_Data), .en(wen_7), .clk(clk), .Q(t2));  // open: clr
  Register #(.width(32)) x11 (.D(Write_Data), .en(wen_11), .clk(clk), .Q(out11));  // open: clr
  Register #(.width(32)) x15 (.D(Write_Data), .en(wen_15), .clk(clk), .Q(out15));  // open: clr
  Register #(.width(32)) x19 (.D(Write_Data), .en(wen_19), .clk(clk), .Q(out19));  // open: clr
  Register #(.width(32)) x23 (.D(Write_Data), .en(wen_23), .clk(clk), .Q(out23));  // open: clr
  Register #(.width(32)) x27 (.D(Write_Data), .en(wen_27), .clk(clk), .Q(out27));  // open: clr
  Register #(.width(32)) x31 (.D(Write_Data), .en(wen_31), .clk(clk), .Q(out31));  // open: clr
  Demultiplexer #(.enable("false"), .select(5)) demultiplexer_1 (
    .out0(wen_0), .out1(wen_1), .out2(wen_2), .out3(wen_3), .out4(wen_4), .out5(wen_5), .out6(wen_6),
    .out7(wen_7), .out8(wen_8), .out9(wen_9), .out10(wen_10), .out11(wen_11), .out12(wen_12), .out13(wen_13),
    .out14(wen_14), .out15(wen_15), .out16(wen_16), .out17(wen_17), .out18(wen_18), .out19(wen_19),
    .out20(wen_20), .out21(wen_21), .out22(wen_22), .out23(wen_23), .out24(wen_24), .out25(wen_25),
    .out26(wen_26), .out27(wen_27), .out28(wen_28), .out29(wen_29), .out30(wen_30), .out31(wen_31),
    .in(RegWEn), .sel(rd));
  Multiplexer #(.enable("false"), .select(5), .width(32)) multiplexer_1 (
    .in0(out0), .in1(ra), .in2(sp), .in3(out3), .in4(out4), .in5(t0), .in6(t1), .in7(t2), .in8(s0), .in9(s1),
    .in10(a0), .in11(out11), .in12(out12), .in13(out13), .in14(out14), .in15(out15), .in16(out16),
    .in17(out17), .in18(out18), .in19(out19), .in20(out20), .in21(out21), .in22(out22), .in23(out23),
    .in24(out24), .in25(out25), .in26(out26), .in27(out27), .in28(out28), .in29(out29), .in30(out30),
    .in31(out31), .out(Read_Data_1), .sel(rs1));
  Multiplexer #(.enable("false"), .select(5), .width(32)) multiplexer_2 (
    .in0(out0), .in1(ra), .in2(sp), .in3(out3), .in4(out4), .in5(t0), .in6(t1), .in7(t2), .in8(s0), .in9(s1),
    .in10(a0), .in11(out11), .in12(out12), .in13(out13), .in14(out14), .in15(out15), .in16(out16),
    .in17(out17), .in18(out18), .in19(out19), .in20(out20), .in21(out21), .in22(out22), .in23(out23),
    .in24(out24), .in25(out25), .in26(out26), .in27(out27), .in28(out28), .in29(out29), .in30(out30),
    .in31(out31), .out(Read_Data_2), .sel(rs2));

  // Other names for the same wires on the sheet: out1[31:0] = ra; out2[31:0] = sp; out5[31:0] = t0; out6[31:0] = t1;
  //   out7[31:0] = t2; out8[31:0] = s0; out9[31:0] = s1; out10[31:0] = a0; read_data1[31:0] = Read_Data_1;
  //   read_data2[31:0] = Read_Data_2; read_reg1[4:0] = rs1; read_reg2[4:0] = rs2; write_en = RegWEn;
  //   write_reg[4:0] = rd

  // Notes on the sheet:
  //   INPUTS to your circuit
  //   DON'T CHANGE THE LOCATIONS OF THE INPUTS AND OUTPUTS!
  //   These are DEBUG/TEST outputs from your circuit.
  //   OUTPUTS from your circuit
endmodule
