// Logisim project cpu-gemini-intergrated-test.circ as structural Verilog: 1 circuit, main circuit run_main
module run_main (
  output [31:0] ra,
  output [31:0] sp,
  output [31:0] t0,
  output [31:0] t1,
  output [31:0] t2,
  output [31:0] s0,
  output [31:0] s1,
  output [31:0] a0,
  output [31:0] Requested_Address,
  output [31:0] Requested_Instruction,
  output [15:0] Time_Step,
  output halt
);

  wire clk;

  Clock clock_1 (.out(clk));
  // Probe on Requested_Address
  // test_harness test_harness_1: pin names not known; wires that end beside it: Requested_Instruction, clk, Requested_Address, ra, sp, t0, t1, t2, s0, s1, a0
  ROM #(.addrWidth(14), .dataWidth(32)) rom_1 (.addr(Requested_Address[15:2]), .data(Requested_Instruction));
  // Probe on Requested_Instruction
  Counter #(.max('hffff), .width(16)) counter_1 (.clk(clk), .Q(Time_Step));  // open: clr, load, up, count, D, carry
  Comparator #(.width(16)) comparator_1 (.a(Time_Step), .b(16'h3d), .eq(halt));  // open: gt, lt

  // Other names for the same wires on the sheet: fetch_addr[31:0] = Requested_Address;
  //   Instruction[31:0] = Requested_Instruction

  // Notes on the sheet:
  //   contents of rom_1 (hex, n*v repeats v):
  //   100002B7 00500313 00300393 007300B3 40730133 02730433 027314B3 00731533 007320B3 00734133 00735433
  //   407354B3 00736533 007370B3 00A30113 00231413 00432493 00134513 00135093 40135113 00836413 00437493
  //   0062A023 0002A083 00729223 00429103 00628423 00828403 000014B7 00002517 00730463 00000013 00630463
  //   0EE00493 00731463 0EE00493 00631463 00000013 0063C463 0EE00493 00734463 00000013 00735463 0EE00493
  //   0063D463 00000013 0063E463 0EE00493 00736463 00000013 00737463 0EE00493 0063F463 00000013 008000EF
  //   0EE00493 00C08167 0EE00493 0AA00493
  //   Instruction Memory
  //   Halts Execution After Constant # of Clock Cycles
  //   Constant
endmodule
